# Fritzing sketch Buttons (saved by Fritzing 0.9.3b)
breadboards: 1

parts:
  Part1 = Arduino Uno (Rev3)
  S1 = Round Pushbutton
  D2 = Rectifier Diode [part_number=1N4001 package="300 mil [THT]"]
  S2 = Round Pushbutton
  S3 = Round Pushbutton
  S4 = Round Pushbutton
  D3 = Rectifier Diode [part_number=1N4001 package="300 mil [THT]"]
  D4 = Rectifier Diode [part_number=1N4001 package="300 mil [THT]"]
  D5 = Rectifier Diode [part_number=1N4001 package="300 mil [THT]"]

nets:
  N1: Part1.GND, S1.leg0, S2.leg0, S3.leg0, S4.leg0
  N2: Part1.D2, D2.anode, D3.anode, D4.anode, D5.anode
  N3: Part1.D4, S4.leg1, D3.cathode
  N4: Part1.D5_PWM, D2.cathode, S3.leg1
  N5: Part1.D6_PWM, S2.leg1, D4.cathode
  N6: Part1.D7, S1.leg1, D5.cathode
